// Logisim project DragonArch.circ as structural Verilog
module ALU (
  input  [3:0] ALU_code,
  input  [15:0] X,
  input  [15:0] Y,
  output [15:0] Out
);

  wire adder_1_cout, adder_2_cout, multiplexer_2_out, subtractor_1_bout, subtractor_2_bout, undriven;
  wire [1:0] undriven_2;
  wire [15:0] adder_1_out, adder_2_out, and_1_out, negator_1_out, or_1_out, subtractor_1_out,
       subtractor_2_out, xor_1_out;

  Adder #(.width(16)) adder_1 (.a(X), .b(X), .out(adder_1_out), .cin(undriven), .cout(adder_1_cout));
  Subtractor #(.width(16)) subtractor_1 (
    .a(X), .b(X), .out(subtractor_1_out), .bin(undriven), .bout(subtractor_1_bout));
  assign and_1_out = X & X;  // AND_Gate and_1, 16 bits wide
  assign or_1_out = X | X;  // OR_Gate or_1, 16 bits wide
  assign xor_1_out = X ^ X;  // XOR_Gate xor_1, 16 bits wide
  Negator #(.width(16)) negator_1 (.in(X), .out(negator_1_out));
  Adder #(.width(16)) adder_2 (.a(X), .b(16'h1), .out(adder_2_out), .cin(undriven), .cout(adder_2_cout));
  Subtractor #(.width(16)) subtractor_2 (
    .a(X), .b(16'h1), .out(subtractor_2_out), .bin(undriven), .bout(subtractor_2_bout));
  Multiplexer #(.select(4), .width(16), .enable("false")) multiplexer_1 (
    .in0(adder_1_out), .in1(subtractor_1_out), .in2(and_1_out), .in3(or_1_out), .in4(xor_1_out),
    .in5(negator_1_out), .in6(X), .in7(adder_2_out), .in8(subtractor_2_out), .out(Out), .sel(ALU_code));  // open: in9, in10, in11, in12, in13, in14, in15
  Multiplexer #(.select(2), .enable("false")) multiplexer_2 (
    .in0(adder_1_cout), .in1(subtractor_1_bout), .in2(adder_2_cout), .in3(subtractor_2_bout),
    .out(multiplexer_2_out), .sel(undriven_2));

  assign Y = X;

  // Notes on the sheet:
  //   CarryIn???
  //   Arithmetic Logic Unit
  //   ???
  //   ???
  //   CarryOut???
endmodule

module GPRs (
  input  Write0,
  input  Write1,
  input  Write2,
  input  [2:0] Select,
  input  [15:0] RegisterIn,
  output [15:0] Read0,
  output [15:0] Read1,
  output [15:0] Read3,
  output [15:0] RegisterOut0,
  output [15:0] RegisterOut1,
  output [15:0] RegisterOut2,
  output [15:0] RegisterOut3,
  output [15:0] RegisterOut4,
  output [15:0] RegisterOut5,
  output [15:0] RegisterOut6,
  output [15:0] RegisterOut7
);

  wire Clock_out, demultiplexer_1_out0, demultiplexer_1_out1, demultiplexer_1_out2, demultiplexer_1_out3,
       demultiplexer_1_out4, demultiplexer_1_out5, demultiplexer_1_out6, demultiplexer_1_out7;

  Demultiplexer #(.select(3), .enable("false")) demultiplexer_1 (
    .out0(demultiplexer_1_out0), .out1(demultiplexer_1_out1), .out2(demultiplexer_1_out2),
    .out3(demultiplexer_1_out3), .out4(demultiplexer_1_out4), .out5(demultiplexer_1_out5),
    .out6(demultiplexer_1_out6), .out7(demultiplexer_1_out7), .in(Write0), .sel(Select));
  Demultiplexer #(.select(3), .enable("false")) demultiplexer_2 (
    .out0(demultiplexer_1_out0), .out1(demultiplexer_1_out1), .out2(demultiplexer_1_out2),
    .out3(demultiplexer_1_out3), .out4(demultiplexer_1_out4), .out5(demultiplexer_1_out5),
    .out6(demultiplexer_1_out6), .out7(demultiplexer_1_out7), .in(Write1), .sel(Select));
  Demultiplexer #(.select(3), .enable("false")) demultiplexer_3 (
    .out0(demultiplexer_1_out0), .out1(demultiplexer_1_out1), .out2(demultiplexer_1_out2),
    .out3(demultiplexer_1_out3), .out4(demultiplexer_1_out4), .out5(demultiplexer_1_out5),
    .out6(demultiplexer_1_out6), .out7(demultiplexer_1_out7), .in(Write2), .sel(Select));
  Register #(.width(16)) Reg0 (
    .D(RegisterIn), .en(demultiplexer_1_out0), .Q(RegisterOut0), .clk(Clock_out));  // open: clr
  Register #(.width(16)) Reg1 (
    .D(RegisterIn), .en(demultiplexer_1_out1), .Q(RegisterOut1), .clk(Clock_out));  // open: clr
  Register #(.width(16)) Reg2 (
    .D(RegisterIn), .en(demultiplexer_1_out2), .Q(RegisterOut2), .clk(Clock_out));  // open: clr
  Register #(.width(16)) Reg3 (
    .D(RegisterIn), .en(demultiplexer_1_out3), .Q(RegisterOut3), .clk(Clock_out));  // open: clr
  Register #(.width(16)) Reg4 (
    .D(RegisterIn), .en(demultiplexer_1_out4), .Q(RegisterOut4), .clk(Clock_out));  // open: clr
  Register #(.width(16)) Reg5 (
    .D(RegisterIn), .en(demultiplexer_1_out5), .Q(RegisterOut5), .clk(Clock_out));  // open: clr
  Register #(.width(16)) Reg6 (
    .D(RegisterIn), .en(demultiplexer_1_out6), .Q(RegisterOut6), .clk(Clock_out));  // open: clr
  Register #(.width(16)) Reg7 (
    .D(RegisterIn), .en(demultiplexer_1_out7), .Q(RegisterOut7), .clk(Clock_out));  // open: clr
  Clock Clock (.out(Clock_out));
  Multiplexer #(.select(3), .width(16), .enable("false")) multiplexer_1 (
    .in0(RegisterOut0), .in1(RegisterOut1), .in2(RegisterOut2), .in3(RegisterOut3), .in4(RegisterOut4),
    .in5(RegisterOut5), .in6(RegisterOut6), .in7(RegisterOut7), .out(Read0), .sel(Select));
  Multiplexer #(.select(3), .width(16), .enable("false")) multiplexer_2 (
    .in0(RegisterOut0), .in1(RegisterOut1), .in2(RegisterOut2), .in3(RegisterOut3), .in4(RegisterOut4),
    .in5(RegisterOut5), .in6(RegisterOut6), .in7(RegisterOut7), .out(Read1), .sel(Select));
  Multiplexer #(.select(3), .width(16), .enable("false")) multiplexer_3 (
    .in0(RegisterOut0), .in1(RegisterOut1), .in2(RegisterOut2), .in3(RegisterOut3), .in4(RegisterOut4),
    .in5(RegisterOut5), .in6(RegisterOut6), .in7(RegisterOut7), .out(Read3), .sel(Select));

  // Notes on the sheet:
  //   General Purpose Registers
endmodule

module IR (
  input  IRLoad,
  input  [15:0] instruction,
  output [3:0] Opcode,
  output [2:0] RegisterSelect0,
  output [2:0] RegisterSelect1,
  output [2:0] RegisterSelect2
);

  wire clock_1_out;
  wire [15:13] IR_q;

  Clock clock_1 (.out(clock_1_out));
  Register #(.width(16)) IR (
    .D(instruction), .en(IRLoad), .Q({IR_q, Opcode, RegisterSelect2, RegisterSelect1, RegisterSelect0}),
    .clk(clock_1_out));  // open: clr

  // Notes on the sheet:
  //   Instruction Register
endmodule

module PC (
  input  [15:0] ImmidiateRegister,
  input  PCLoad,
  input  PCReset,
  input  [15:0] S_Register,
  input  [1:0] PCSelect,
  output [15:0] PCOut
);

  wire clock_1_out;
  wire [15:0] adder_1_out, adder_2_out, multiplexer_1_out;

  Adder #(.width(16)) adder_1 (.a(PCOut), .b(16'h1), .out(adder_1_out));  // open: cin, cout
  Adder #(.width(16)) adder_2 (.a(PCOut), .b(ImmidiateRegister), .out(adder_2_out));  // open: cin, cout
  Multiplexer #(.select(2), .width(16), .enable("false")) multiplexer_1 (
    .in0(adder_1_out), .in1(ImmidiateRegister), .in2(adder_2_out), .in3(S_Register), .out(multiplexer_1_out),
    .sel(PCSelect));
  Clock clock_1 (.out(clock_1_out));
  Register #(.width(16)) PCReg (.D(multiplexer_1_out), .en(PCLoad), .Q(PCOut), .clk(clock_1_out), .clr(PCReset));

  // Notes on the sheet:
  //   Program Counter
endmodule
